# Fritzing sketch Task2_Servo-3_Nano_HC05 (saved by Fritzing 0.9.3b)

parts:
  Part1 = Arduino Nano (Rev3.0)
  SG-90(S1) = Basic Servo
  SG-90(S2) = Basic Servo
  SG-90(S3) = Basic Servo
  Part3 = Bluetooth HC-05 Macho
  U1 = LIPO-110mAh [package=lipo-110]
  U2 = LIPO-110mAh [package=lipo-110]
  J1 = Infrared Proximity Sensor

nets:
  N1: Part1.D1/TX, Part3.TXD
  N2: Part1.D0/RX, Part3.RXD
  GND: Part1.GND, Part3.GND, U2.-, J1.GND
  N3: Part1.D7, SG-90(S1).pulse
  N4: Part1.D8, SG-90(S2).pulse
  N5: Part1.D9, SG-90(S3).pulse
  N6: Part1.VIN, U1.+
  VCC: Part1.5V, Part3.VCC, J1.Vcc
  N7: Part1.A0, J1.Vout
  GND_2: SG-90(S1).gnd, SG-90(S2).gnd, SG-90(S3).gnd
  VCC_2: SG-90(S1).vcc, SG-90(S2).vcc, SG-90(S3).vcc
  N8: U1.-, U2.+

notes:
  INTERFACING ARDUINO-NAN0 withHC05, Sharp-Sensor and Servo-Motors for
